// Logisim project 1.2) Contrôle de parité.circ as structural Verilog: 1 circuit, main circuit main
module main (
  input  e0,
  input  e1,
  input  e2,
  input  in_4,
  input  in_5,
  input  in_6,
  output s,
  output out_8
);

  wire and_1_out, and_2_out, and_3_out, and_4_out, not_1_out, not_2_out, not_3_out, not_4_out, not_5_out,
       not_6_out;

  not not_1 (not_1_out, e0);
  not not_2 (not_2_out, e1);
  not not_3 (not_3_out, e0);
  not not_4 (not_4_out, e2);
  not not_5 (not_5_out, e1);
  not not_6 (not_6_out, e2);
  and and_1 (and_1_out, not_1_out, not_2_out, e2);
  and and_2 (and_2_out, not_3_out, e1, not_4_out);
  and and_3 (and_3_out, e0, not_5_out, not_6_out);
  and and_4 (and_4_out, e0, e1, e2);
  ExactlyOne xor_1 (.out(out_8), .in0(in_4), .in2(in_5), .in4(in_6));
  or or_1 (s, and_1_out, and_2_out, and_3_out, and_4_out);
endmodule
